# Fritzing sketch schematic (saved by Fritzing 0.8.6b)
breadboards: 1

parts:
  Part1 = Arduino Uno (Rev3)
  R1 = Resistor [tolerance=±5% resistance=330 package=THT]
  R2 = Resistor [tolerance=±5% resistance=330 package=THT]
  LED1 = LED - 3mm [color="Red (633nm)" package="3 mm [THT]"]
  LED2 = LED - 3mm [color="Red (633nm)" package="3 mm [THT]"]

nets:
  N1: Part1.D12/MISO, LED1.anode
  N2: Part1.D13/SCK, LED2.anode
  N3: Part1.GND, R1.Pin_0, R2.Pin_0
  N4: R1.Pin_1, LED2.cathode
  N5: R2.Pin_1, LED1.cathode
